# Fritzing sketch Ultrasonic.robot (saved by Fritzing 0.9.3b)
breadboards: 1

parts:
  Part1 = Arduino Uno (Rev3)
  J1 = Piezo Speaker
  hc-sr1 = hc-sr04
  Part2 = LED Matrix - Serial Interface - Red/Green/Blue
  Part3 = LED Matrix - Serial Interface - Red/Green/Blue
  LED1 = RGB LED (com. cathode, rgb) [package="5 mm [THT]"]
  LED2 = RGB LED (com. cathode, rgb) [package="5 mm [THT]"]  # not connected
  LED3 = RGB LED (com. cathode, rgb) [package="5 mm [THT]"]  # not connected
  R1 = Resistor [tolerance=±5% resistance=220 package="1206 [SMD]"]
  R2 = Resistor [tolerance=±5% resistance=220 package="1206 [SMD]"]
  R3 = Resistor [tolerance=±5% resistance=220 package="1206 [SMD]"]

nets:
  VCC: Part1.A4/SDA, Part1.5V, J1.pin2, hc-sr1.VCC, Part2.VCC, Part2.SCK, Part3.VCC
  N1: Part1.A5/SCL, Part2.CS
  N2: Part1.D11_PWM/MOSI, hc-sr1.Echo
  N3: Part1.D12/MISO, Part3.MISO
  GND: Part1.GND, J1.pin1, hc-sr1.GND, Part2.GND, Part3.GND, LED1.common_cathode
  N4: Part1.D3_PWM, Part2.MISO
  N5: Part1.D4, Part3.CS
  N6: Part1.D6_PWM, hc-sr1.Trig
  N7: LED1.red_anode, R3.Pin_0
  N8: LED1.green_anode, R2.Pin_0
  N9: LED1.blue_anode, R1.Pin_1

notes:
  All of the pins along the blue/violet line are connected to GND
  All of the pins along the red line are connected to 5V
